# Fritzing sketch Circuit (saved by Fritzing 0.9.3b)

parts:
  Part1 = Arduino Uno (Rev3) - ICSP
  GSM_SIM_GPSR_SMS_SIM900_SIM1 = SIM800L [package=THT]
  U1 = SUP500F [package=sup500f]
  Part2 = Triple Axis Accelerometer Breakout - ADXL345
  VCC1 = Battery
  R1 = Resistor [tolerance=±5% resistance=2.2 package="0402 [SMD]"]

nets:
  N1: Part1.A4/SDA, Part2.SDA
  N2: Part1.A5/SCL, Part2.SCL
  N3: Part1.D10_PWM/SS, GSM_SIM_GPSR_SMS_SIM900_SIM1.SIM_TXD
  GND: Part1.GND, GSM_SIM_GPSR_SMS_SIM900_SIM1.GND, U1.GND, Part2.GND, VCC1.-
  N4: Part1.D0/RX, U1.RX-I
  N5: Part1.D1/TX, U1.TX-O
  3V3: Part1.3V3, U1.VCC
  5V: Part1.5V, Part2.VCC
  N6: Part1.VIN, VCC1.+, R1.Pin_0
  N7: GSM_SIM_GPSR_SMS_SIM900_SIM1.5V, R1.Pin_1
